// Logisim project Boletín 2 HUGO .circ as structural Verilog: 8 circuits, main circuit main
module main (
  input  [3:0] in_1,
  input  [3:0] in_2,
  input  Interruptor,
  input  [3:0] in_4,
  output Acarreo,
  output [3:0] out_6
);

  wire adder_1_cout, adder_2_cout, adder_4_cout, and_1_out, and_2_out, or_1_out, or_3_out;
  wire [3:0] adder_1_out, adder_2_out, adder_3_out, adder_4_out;

  Adder #(.width(4)) adder_1 (.a(in_1), .b(in_2), .out(adder_1_out), .cout(adder_1_cout));  // open: cin
  Adder #(.width(4)) adder_2 (.a(in_1), .b(in_2), .out(adder_2_out), .cout(adder_2_cout));  // open: cin
  Adder #(.width(4)) adder_3 (.a(in_1), .b(in_2), .out(adder_3_out));  // open: cin, cout
  Adder #(.width(4)) adder_4 (.a(adder_3_out), .b(in_4), .out(adder_4_out), .cout(adder_4_cout));  // open: cin
  and and_1 (and_1_out, adder_1_out[3], adder_1_out[1]);
  and and_2 (and_2_out, adder_1_out[3], adder_1_out[2]);
  or or_1 (or_1_out, and_1_out, and_2_out);
  or or_2 (Acarreo, adder_2_cout, adder_4_cout);
  Multiplexer #(.width(4)) multiplexer_1 (
    .in0(adder_2_out), .in1(adder_4_out), .out(out_6), .sel(or_3_out), .en(Interruptor));
  or or_3 (or_3_out, or_1_out, adder_1_cout);
endmodule

module Ejercicio_1 (
  input  [3:0] Numero_1,
  input  [3:0] Numero_2,
  input  Interruptor,
  input  [3:0] _6,
  output [3:0] \Solución ,
  output Acarreo
);

  wire adder_1_cout, adder_2_cout, and_1_out, and_2_out, or_1_out, or_3_out;
  wire [3:0] adder_1_out, adder_2_out;

  Adder #(.width(4)) adder_1 (.a(Numero_1), .b(Numero_2), .out(adder_1_out), .cout(adder_1_cout));  // open: cin
  Adder #(.width(4)) adder_2 (.a(adder_1_out), .b(_6), .out(adder_2_out), .cout(adder_2_cout));  // open: cin
  and and_1 (and_1_out, adder_1_out[3], adder_1_out[1]);
  and and_2 (and_2_out, adder_1_out[3], adder_1_out[2]);
  or or_1 (or_1_out, and_1_out, and_2_out);
  Multiplexer #(.width(4)) multiplexer_1 (
    .in0(adder_1_out), .in1(adder_2_out), .out(\Solución ), .sel(or_3_out), .en(Interruptor));
  or or_2 (Acarreo, adder_1_cout, adder_2_cout);
  or or_3 (or_3_out, or_1_out, adder_1_cout);
endmodule

module Ejercicio_2 (
  input  in_1,
  input  [3:0] in_2,
  input  in_3,
  input  [3:0] A,
  input  [3:0] B,
  input  [3:0] C,
  output [3:0] out_7,
  output out_8
);

  wire comparator_1_gt;
  wire [3:0] multiplexer_1_out;

  Multiplexer #(.width(4)) multiplexer_1 (.in0(B), .in1(C), .out(multiplexer_1_out), .sel(comparator_1_gt), .en(in_3));
  Comparator #(.width(4), .mode("unsigned")) comparator_1 (.a(B), .b(C), .gt(comparator_1_gt));  // open: eq, lt
  Ejercicio_1 ejercicio_1_1 (
    .Numero_1(A), .Numero_2(multiplexer_1_out), ._6(in_2), .\Solución (out_7), .Acarreo(out_8),
    .Interruptor(in_1));
endmodule

module Ejercicio_3 (
  input  [3:0] A,
  input  [3:0] B,
  input  [1:0] C1_C2,
  output [3:0] out_4,
  output Overflow
);

  wire adder_1_cout, adder_3_cout, and_1_out, and_2_out, and_3_out, and_4_out, and_5_out, and_6_out,
       and_7_out, and_8_out, and_9_out, not_3_out, not_4_out, not_5_out, not_6_out, not_7_out, not_8_out,
       not_9_out, not_10_out, not_11_out, not_12_out, not_13_out, not_14_out, not_15_out, not_16_out,
       not_17_out, or_1_out, or_2_out, or_3_out, or_4_out, or_5_out;
  wire [3:0] adder_1_out, adder_2_out, adder_3_out, adder_4_out, adder_5_out, adder_6_out, adder_7_out,
       not_1_out, not_2_out;

  assign not_1_out = ~B;  // NOT_Gate not_1, 4 bits wide
  assign not_2_out = ~B;  // NOT_Gate not_2, 4 bits wide
  Adder #(.width(4)) adder_1 (.a(A), .b(B), .out(adder_1_out), .cout(adder_1_cout));  // open: cin
  Adder #(.width(4)) adder_2 (.a(A), .b(B), .out(adder_2_out));  // open: cin, cout
  Adder #(.width(4)) adder_3 (.a(A), .b(not_1_out), .out(adder_3_out), .cout(adder_3_cout));  // open: cin
  Adder #(.width(4)) adder_4 (.a(4'b0001), .b(not_2_out), .out(adder_4_out));  // open: cin, cout
  Adder #(.width(4)) adder_5 (.a(adder_4_out), .b(A), .out(adder_5_out));  // open: cin, cout
  Adder #(.width(4)) adder_6 (.a(adder_1_out), .b(4'b0000), .out(adder_6_out), .cin(adder_1_cout));  // open: cout
  Adder #(.width(4)) adder_7 (.a(adder_3_out), .b(4'b0000), .out(adder_7_out), .cin(adder_3_cout));  // open: cout
  not not_3 (not_3_out, adder_6_out[3]);
  not not_4 (not_4_out, A[3]);
  not not_5 (not_5_out, B[3]);
  not not_6 (not_6_out, adder_2_out[3]);
  not not_7 (not_7_out, B[3]);
  not not_8 (not_8_out, A[3]);
  not not_9 (not_9_out, adder_5_out[3]);
  not not_10 (not_10_out, adder_4_out[3]);
  not not_11 (not_11_out, A[3]);
  and and_1 (and_1_out, not_3_out, A[3], B[3]);
  and and_2 (and_2_out, adder_6_out[3], not_4_out, not_5_out);
  and and_3 (and_3_out, not_6_out, B[3], A[3]);
  and and_4 (and_4_out, not_7_out, not_8_out, adder_2_out[3]);
  not not_12 (not_12_out, adder_7_out[3]);
  and and_5 (and_5_out, A[3], not_12_out, not_1_out[3]);
  not not_13 (not_13_out, A[3]);
  not not_14 (not_14_out, not_1_out[3]);
  and and_6 (and_6_out, not_13_out, not_14_out, adder_7_out[3]);
  and and_7 (and_7_out, not_9_out, adder_4_out[3], A[3]);
  and and_8 (and_8_out, not_10_out, not_11_out, adder_5_out[3]);
  not not_15 (not_15_out, B[2]);
  not not_16 (not_16_out, B[1]);
  not not_17 (not_17_out, B[0]);
  or or_1 (or_1_out, and_1_out, and_2_out);
  or or_2 (or_2_out, and_3_out, and_4_out);
  or or_3 (or_3_out, and_5_out, and_6_out);
  or or_4 (or_4_out, and_7_out, and_8_out);
  and and_9 (and_9_out, B[3], not_15_out, not_16_out, not_17_out);
  or or_5 (or_5_out, or_4_out, and_9_out);
  Multiplexer #(.select(2), .width(4)) multiplexer_1 (
    .in0(adder_6_out), .in1(adder_2_out), .in2(adder_7_out), .in3(adder_5_out), .out(out_4), .sel(C1_C2),
    .en(1'b1));
  Multiplexer #(.select(2)) multiplexer_2 (
    .in0(or_1_out), .in1(or_2_out), .in2(or_3_out), .in3(or_5_out), .out(Overflow), .sel(C1_C2), .en(1'b1));

  // Notes on the sheet:
  //   suma/resta
endmodule

module Ejercicio_4 (
  input  [3:0] A,
  input  [3:0] B,
  input  [3:0] C,
  output [1:0] N,
  output [3:0] S
);

  wire and_2_out, comparator_1_eq, comparator_2_eq, comparator_3_eq, not_1_out, not_2_out, not_3_out,
       or_2_out;
  wire [3:0] ejercicio4_b_1_out_2, ejercicio4_b_2_out_2, ejercicio4_b_3_out_2, multiplexer_1_out,
       multiplexer_2_out;

  Ejercicio4_B ejercicio4_b_1 (.Entrada(A), .out_2(ejercicio4_b_1_out_2));
  Ejercicio4_B ejercicio4_b_2 (.Entrada(B), .out_2(ejercicio4_b_2_out_2));
  Ejercicio4_B ejercicio4_b_3 (.Entrada(C), .out_2(ejercicio4_b_3_out_2));
  Comparator #(.width(4)) comparator_1 (
    .a(ejercicio4_b_1_out_2), .b(ejercicio4_b_2_out_2), .eq(comparator_1_eq));  // open: gt, lt
  Comparator #(.width(4)) comparator_2 (
    .a(ejercicio4_b_1_out_2), .b(ejercicio4_b_3_out_2), .eq(comparator_2_eq));  // open: gt, lt
  Comparator #(.width(4)) comparator_3 (
    .a(ejercicio4_b_2_out_2), .b(ejercicio4_b_3_out_2), .eq(comparator_3_eq));  // open: gt, lt
  and and_1 (N[0], comparator_1_eq, comparator_2_eq);
  or or_1 (N[1], comparator_1_eq, comparator_2_eq, comparator_3_eq);
  or or_2 (or_2_out, comparator_1_eq, comparator_2_eq, comparator_3_eq);
  not not_1 (not_1_out, comparator_2_eq);
  Multiplexer #(.width(4)) multiplexer_1 (
    .in0(ejercicio4_b_1_out_2), .in1(ejercicio4_b_2_out_2), .out(multiplexer_1_out), .sel(not_1_out),
    .en(1'b1));
  not not_2 (not_2_out, comparator_2_eq);
  not not_3 (not_3_out, comparator_1_eq);
  and and_2 (and_2_out, not_2_out, not_3_out);
  Multiplexer #(.width(4)) multiplexer_2 (
    .in0(multiplexer_1_out), .in1(ejercicio4_b_3_out_2), .out(multiplexer_2_out), .sel(and_2_out), .en(1'b1));
  Multiplexer #(.width(4)) multiplexer_3 (.in0(4'b0000), .in1(multiplexer_2_out), .out(S), .sel(or_2_out), .en(1'b1));
endmodule

module Ejercicio_5 (
  input  [3:0] A,
  input  [3:0] B,
  input  C1_C2,
  output A_B,
  output A_B_2,
  output A_B_3
);

  wire comparator_1_eq, comparator_1_gt, comparator_1_lt, comparator_2_eq, comparator_2_gt, comparator_2_lt;
  wire [3:0] ejercicio4_b_1_out_2, ejercicio4_b_2_out_2, multiplexer_1_out, multiplexer_2_out;

  Ejercicio4_B ejercicio4_b_1 (.Entrada(A), .out_2(ejercicio4_b_1_out_2));
  Ejercicio4_B ejercicio4_b_2 (.Entrada(B), .out_2(ejercicio4_b_2_out_2));
  Multiplexer #(.width(4)) multiplexer_1 (
    .in0(ejercicio4_b_1_out_2), .in1(A), .out(multiplexer_1_out), .sel(C1_C2), .en(1'b1));
  Multiplexer #(.width(4)) multiplexer_2 (
    .in0(ejercicio4_b_2_out_2), .in1(B), .out(multiplexer_2_out), .sel(C1_C2), .en(1'b1));
  Comparator #(.width(1), .mode("unsigned")) comparator_1 (
    .a(multiplexer_1_out[3]), .b(multiplexer_2_out[3]), .gt(comparator_1_gt), .eq(comparator_1_eq),
    .lt(comparator_1_lt));
  and and_1 (A_B_2, comparator_2_eq, comparator_1_eq);
  Comparator #(.width(3), .mode("unsigned")) comparator_2 (
    .a(multiplexer_1_out[2:0]), .b(multiplexer_2_out[2:0]), .gt(comparator_2_gt), .eq(comparator_2_eq),
    .lt(comparator_2_lt));
  or or_1 (A_B, comparator_1_gt, comparator_2_lt);
  or or_2 (A_B_3, comparator_2_gt, comparator_1_lt);
endmodule

module Ejercicio4_B (
  input  [3:0] Entrada,
  output [3:0] out_2
);

  wire comparator_1_eq;
  wire [3:0] not_1_out;

  Comparator #(.width(4), .mode("unsigned")) comparator_1 (
    .a(Entrada), .b(4'b1111), .eq(comparator_1_eq));  // open: gt, lt
  Multiplexer #(.width(4)) multiplexer_1 (
    .in0(Entrada), .in1(not_1_out), .out(out_2), .sel(comparator_1_eq), .en(1'b1));
  assign not_1_out = ~Entrada;  // NOT_Gate not_1, 4 bits wide
endmodule

module pasar_c1_a_c2 (
  input  [3:0] entrada,
  output [3:0] out_2
);

  wire and_1_out;
  wire [3:0] adder_1_out;

  and and_1 (and_1_out, entrada[3], 1'b1);
  Adder #(.width(4)) adder_1 (.a(4'b0001), .b(entrada), .out(adder_1_out));  // open: cin, cout
  Multiplexer #(.width(4)) multiplexer_1 (.in0(entrada), .in1(adder_1_out), .out(out_2), .sel(and_1_out), .en(1'b1));
endmodule
