// Logisim project Boletin 2.circ as structural Verilog
module Ejercicio_1 (
  input  [3:0] A,
  input  [3:0] B,
  input  interruptor,
  input  [3:0] plus_6,
  output bit_acarreo,
  output [3:0] salida
);

  wire adder_1_cout, adder_2_cout, and_1_out, and_2_out, or_1_out, or_2_out;
  wire [3:0] adder_1_out, adder_2_out;

  Adder #(.width(4)) adder_1 (.a(A), .b(B), .out(adder_1_out), .cout(adder_1_cout));  // open: cin
  Adder #(.width(4)) adder_2 (.a(adder_1_out), .b(plus_6), .out(adder_2_out), .cout(adder_2_cout));  // open: cin
  and and_1 (and_1_out, adder_1_out[3], adder_1_out[1]);
  and and_2 (and_2_out, adder_1_out[2], adder_1_out[3]);
  or or_1 (or_1_out, and_1_out, and_2_out);
  Multiplexer #(.width(4)) multiplexer_1 (
    .in0(adder_1_out), .in1(adder_2_out), .out(salida), .sel(or_2_out), .en(interruptor));
  or or_2 (or_2_out, or_1_out, adder_1_cout);
  or or_3 (bit_acarreo, adder_1_cout, adder_2_cout);

  // Notes on the sheet:
  //   comparador
  //   menor que 9
  //   mayor que 9
endmodule

module Ejercicio_2 (
  input  [3:0] _6_SIEMPRE,
  input  INTERRUPTOR_SUMA,
  input  interruptor,
  input  [3:0] A,
  input  [3:0] B,
  input  [3:0] C,
  output ACARREO,
  output [3:0] Resultado
);

  wire comparator_1_gt;
  wire [3:0] multiplexer_1_out;

  Multiplexer #(.width(4)) multiplexer_1 (
    .in0(B), .in1(C), .out(multiplexer_1_out), .sel(comparator_1_gt), .en(interruptor));
  Comparator #(.width(4), .mode("unsigned")) comparator_1 (.a(B), .b(C), .gt(comparator_1_gt));  // open: eq, lt
  Ejercicio_1 ejercicio_1_1 (
    .plus_6(_6_SIEMPRE), .A(multiplexer_1_out), .B(A), .bit_acarreo(ACARREO), .salida(Resultado),
    .interruptor(INTERRUPTOR_SUMA));

  // Notes on the sheet:
  //   1 siempre
endmodule

module ejercicio_3 (
  input  [3:0] A,
  input  [3:0] B,
  input  [1:0] c1_c2,
  output [3:0] out_4,
  output overflow
);

  wire adder_1_cout, adder_3_cout, and_1_out, and_2_out, and_3_out, and_4_out, and_5_out, and_6_out,
       and_7_out, and_8_out, and_9_out, not_3_out, not_4_out, not_5_out, not_6_out, not_7_out, not_8_out,
       not_9_out, not_10_out, not_11_out, not_12_out, not_13_out, not_14_out, or_1_out, or_2_out, or_3_out,
       or_4_out, or_5_out;
  wire [3:0] adder_1_out, adder_2_out, adder_3_out, adder_4_out, adder_5_out, adder_6_out, adder_7_out,
       not_1_out, not_2_out;

  assign not_1_out = ~B;  // NOT_Gate not_1, 4 bits wide
  assign not_2_out = ~B;  // NOT_Gate not_2, 4 bits wide
  Adder #(.width(4)) adder_1 (.a(A), .b(B), .out(adder_1_out), .cout(adder_1_cout));  // open: cin
  Adder #(.width(4)) adder_2 (.a(A), .b(B), .out(adder_2_out));  // open: cin, cout
  Adder #(.width(4)) adder_3 (.a(A), .b(not_1_out), .out(adder_3_out), .cout(adder_3_cout));  // open: cin
  Adder #(.width(4)) adder_4 (.a(4'b0001), .b(not_2_out), .out(adder_4_out));  // open: cin, cout
  Adder #(.width(4)) adder_5 (.a(adder_1_out), .b(4'b0000), .out(adder_5_out), .cin(adder_1_cout));  // open: cout
  Adder #(.width(4)) adder_6 (.a(adder_3_out), .b(4'b0000), .out(adder_6_out), .cin(adder_3_cout));  // open: cout
  Adder #(.width(4)) adder_7 (.a(adder_4_out), .b(A), .out(adder_7_out));  // open: cin, cout
  not not_3 (not_3_out, adder_7_out[3]);
  not not_4 (not_4_out, A[3]);
  not not_5 (not_5_out, adder_4_out[3]);
  and and_1 (and_1_out, A[3], B[3], not_6_out);
  not not_6 (not_6_out, adder_5_out[3]);
  not not_7 (not_7_out, A[3]);
  and and_2 (and_2_out, not_7_out, not_8_out, adder_5_out[3]);
  not not_8 (not_8_out, B[3]);
  and and_3 (and_3_out, A[3], B[3], not_9_out);
  not not_9 (not_9_out, adder_2_out[3]);
  not not_10 (not_10_out, A[3]);
  not not_11 (not_11_out, B[3]);
  and and_4 (and_4_out, not_10_out, not_11_out, adder_2_out[3]);
  and and_5 (and_5_out, A[3], not_1_out[3], not_12_out);
  not not_12 (not_12_out, adder_6_out[3]);
  not not_13 (not_13_out, A[3]);
  and and_6 (and_6_out, not_13_out, not_14_out, adder_6_out[3]);
  not not_14 (not_14_out, not_1_out[3]);
  and and_7 (and_7_out, A[3], adder_4_out[3], not_3_out);
  or or_1 (or_1_out, and_7_out, and_8_out);
  and and_8 (and_8_out, not_4_out, not_5_out, adder_7_out[3]);
  or or_2 (or_2_out, and_1_out, and_2_out);
  or or_3 (or_3_out, and_3_out, and_4_out);
  or or_4 (or_4_out, and_5_out, and_6_out);
  or or_5 (or_5_out, or_1_out, and_9_out);
  and and_9 (and_9_out, B[3], ~B[2], ~B[1], ~B[0]);  // AND_Gate
  Multiplexer #(.select(2), .width(4)) multiplexer_1 (
    .in0(adder_5_out), .in1(adder_2_out), .in2(adder_6_out), .in3(adder_7_out), .out(out_4), .sel(c1_c2),
    .en(1'b1));
  Multiplexer #(.select(2)) multiplexer_2 (
    .in0(or_2_out), .in1(or_3_out), .in2(or_4_out), .in3(or_5_out), .out(overflow), .sel(c1_c2), .en(1'b1));

  // Notes on the sheet:
  //   Sumador C1
  //   Sumador C2
  //   Restador C1
  //   Restador C2
  //   suma/resta
endmodule

module ejercicio_4 (
  input  [3:0] A,
  input  [3:0] B,
  input  [3:0] C,
  output [1:0] N,
  output [3:0] S
);

  wire and_1_out, and_2_out, comparator_1_eq, comparator_2_eq, comparator_3_eq, not_1_out, not_2_out,
       not_3_out, or_3_out;
  wire [3:0] multiplexer_1_out, multiplexer_2_out, n1111_a_0000_1_s, n1111_a_0000_2_s, n1111_a_0000_3_s;

  _1111_a_0000 u_1111_a_0000_1 (.entrada(A), .S(n1111_a_0000_1_s));
  _1111_a_0000 u_1111_a_0000_2 (.entrada(B), .S(n1111_a_0000_2_s));
  _1111_a_0000 u_1111_a_0000_3 (.entrada(C), .S(n1111_a_0000_3_s));
  Comparator #(.width(4)) comparator_1 (
    .a(n1111_a_0000_1_s), .b(n1111_a_0000_2_s), .eq(comparator_1_eq));  // open: gt, lt
  Comparator #(.width(4)) comparator_2 (
    .a(n1111_a_0000_1_s), .b(n1111_a_0000_3_s), .eq(comparator_2_eq));  // open: gt, lt
  Comparator #(.width(4)) comparator_3 (
    .a(n1111_a_0000_2_s), .b(n1111_a_0000_3_s), .eq(comparator_3_eq));  // open: gt, lt
  and and_1 (and_1_out, comparator_1_eq, comparator_2_eq);
  or or_1 (N[1], comparator_1_eq, comparator_2_eq, comparator_3_eq);
  not not_1 (not_1_out, comparator_2_eq);
  buf or_2 (N[0], and_1_out);  // OR_Gate
  not not_2 (not_2_out, comparator_1_eq);
  not not_3 (not_3_out, comparator_2_eq);
  and and_2 (and_2_out, not_2_out, not_3_out);
  Multiplexer #(.width(4)) multiplexer_1 (
    .in0(n1111_a_0000_1_s), .in1(n1111_a_0000_2_s), .out(multiplexer_1_out), .sel(not_1_out), .en(1'b1));
  Multiplexer #(.width(4)) multiplexer_2 (
    .in0(multiplexer_1_out), .in1(n1111_a_0000_3_s), .out(multiplexer_2_out), .sel(and_2_out), .en(1'b1));
  or or_3 (or_3_out, comparator_1_eq, comparator_2_eq, comparator_3_eq);
  Multiplexer #(.width(4)) multiplexer_3 (.in0(4'b0000), .in1(multiplexer_2_out), .out(S), .sel(or_3_out), .en(1'b1));
endmodule

module _1111_a_0000 (
  input  [3:0] entrada,
  output [3:0] S
);

  wire comparator_1_eq;
  wire [3:0] not_1_out;

  Comparator #(.width(4), .mode("unsigned")) comparator_1 (
    .a(entrada), .b(4'b1111), .eq(comparator_1_eq));  // open: gt, lt
  Multiplexer #(.width(4)) multiplexer_1 (.in0(entrada), .in1(not_1_out), .out(S), .sel(comparator_1_eq), .en(1'b1));
  assign not_1_out = ~entrada;  // NOT_Gate not_1, 4 bits wide
endmodule
