// Logisim project Boletin 3.circ as structural Verilog: 6 circuits, main circuit Ejercicio 1
module Ejercicio_1 (
  input  I1,
  input  I0,
  output L,
  output D
);

  wire and_1_out, and_2_out, and_3_out, and_4_out, and_5_out, and_6_out, and_7_out, and_8_out, and_9_out,
       and_10_out, and_11_out, and_12_out, and_13_out, clock_1_out, or_1_out, or_2_out, or_3_out, Q0_q, Q1_q;

  Clock clock_1 (.out(clock_1_out));
  D_Flip_Flop Q2 (.clk(clock_1_out), .D(or_1_out), .Q(L));  // open: Qn, preset, en, reset
  D_Flip_Flop Q1 (.clk(clock_1_out), .D(or_2_out), .Q(Q1_q));  // open: Qn, preset, en, reset
  D_Flip_Flop Q0 (.clk(clock_1_out), .D(or_3_out), .Q(Q0_q));  // open: Qn, preset, en, reset
  and and_1 (and_1_out, I1, I0);
  and and_2 (and_2_out, ~L, Q0_q, I1);  // AND_Gate
  and and_3 (and_3_out, Q1_q, I0);
  and and_4 (and_4_out, Q1_q, I1);
  and and_5 (and_5_out, L, I1, ~I0);  // AND_Gate
  and and_6 (and_6_out, Q1_q, ~I1, ~I0);  // AND_Gate
  and and_7 (and_7_out, ~Q1_q, ~Q0_q, I1, ~I0);  // AND_Gate
  and and_8 (and_8_out, ~L, Q0_q, ~I1, I0);  // AND_Gate
  and and_9 (and_9_out, L, I0);
  and and_10 (and_10_out, I1, I0);
  and and_11 (and_11_out, Q1_q, I1);
  and and_12 (and_12_out, ~Q1_q, ~Q0_q, I0);  // AND_Gate
  and and_13 (and_13_out, ~L, Q0_q, ~I1, ~I0);  // AND_Gate
  or or_1 (or_1_out, and_1_out, and_2_out, and_3_out, and_4_out);
  or or_2 (or_2_out, and_5_out, and_6_out, and_7_out, and_8_out);
  or or_3 (or_3_out, and_9_out, and_10_out, and_11_out, and_12_out, and_13_out);
  and and_14 (D, L, Q0_q);
endmodule

module Ejercicio_2 (
  input  C0,
  input  C1,
  output S1__sube,
  output S0__baja
);

  wire and_1_out, and_2_out, and_3_out, and_4_out, and_5_out, and_6_out, and_7_out, and_8_out, and_9_out,
       and_10_out, clock_1_out, Q0_q, Q1_q;

  Clock clock_1 (.out(clock_1_out));
  J_K_Flip_Flop Q0 (.J(and_1_out), .clk(clock_1_out), .K(and_2_out), .Q(Q0_q));  // open: Qn, preset, en, reset
  J_K_Flip_Flop Q1 (.J(and_3_out), .clk(clock_1_out), .K(and_4_out), .Q(Q1_q));  // open: Qn, preset, en, reset
  and and_1 (and_1_out, ~Q0_q, C0);  // AND_Gate
  and and_2 (and_2_out, Q0_q, ~C0);  // AND_Gate
  and and_3 (and_3_out, ~Q1_q, C1);  // AND_Gate
  and and_4 (and_4_out, Q1_q, ~C1);  // AND_Gate
  and and_5 (and_5_out, ~Q1_q, C1);  // AND_Gate
  and and_6 (and_6_out, ~Q1_q, ~Q0_q, C0);  // AND_Gate
  and and_7 (and_7_out, ~Q0_q, C1, C0);  // AND_Gate
  and and_8 (and_8_out, Q1_q, ~C1);  // AND_Gate
  and and_9 (and_9_out, Q0_q, ~C1, ~C0);  // AND_Gate
  and and_10 (and_10_out, Q1_q, Q0_q, ~C0);  // AND_Gate
  or or_1 (S1__sube, and_5_out, and_6_out, and_7_out);
  or or_2 (S0__baja, and_8_out, and_9_out, and_10_out);
endmodule

module ejercicio_3 (
  input  B0,
  input  B1,
  input  B2,
  input  B3,
  input  [1:0] selector_mux,
  input  reloj,
  input  clear,
  output [3:0] salida
);

  wire multiplexer_1_out, multiplexer_2_out, multiplexer_3_out, multiplexer_4_out;

  Multiplexer #(.select(2)) multiplexer_1 (
    .in0(salida[0]), .in1(salida[2]), .in2(salida[3]), .in3(B0), .out(multiplexer_1_out), .sel(selector_mux),
    .en(1'b1));
  D_Flip_Flop d_ff_1 (.clk(reloj), .D(multiplexer_1_out), .Q(salida[3]), .reset(clear));  // open: Qn, preset, en
  Multiplexer #(.select(2)) multiplexer_2 (
    .in0(salida[3]), .in1(salida[1]), .in2(salida[2]), .in3(B1), .out(multiplexer_2_out), .sel(selector_mux),
    .en(1'b1));
  D_Flip_Flop d_ff_2 (.clk(reloj), .D(multiplexer_2_out), .Q(salida[2]), .reset(clear));  // open: Qn, preset, en
  Multiplexer #(.select(2)) multiplexer_3 (
    .in0(salida[2]), .in1(salida[0]), .in2(salida[1]), .in3(B2), .out(multiplexer_3_out), .sel(selector_mux),
    .en(1'b1));
  D_Flip_Flop d_ff_3 (.clk(reloj), .D(multiplexer_3_out), .Q(salida[1]), .reset(clear));  // open: Qn, preset, en
  Multiplexer #(.select(2)) multiplexer_4 (
    .in0(salida[1]), .in1(salida[3]), .in2(salida[0]), .in3(B3), .out(multiplexer_4_out), .sel(selector_mux),
    .en(1'b1));
  D_Flip_Flop d_ff_4 (.clk(reloj), .D(multiplexer_4_out), .Q(salida[0]), .reset(clear));  // open: Qn, preset, en
endmodule

module b (
  input  in_1,
  input  in_2,
  input  in_3,
  input  in_4,
  output [3:0] out_5,
  output [1:0] out_6,
  output [1:0] out_7,
  output [2:0] out_8
);

  wire and_1_out, and_2_out, clock_1_out, not_1_out, t_ff_1_qn, t_ff_2_qn;

  Clock clock_1 (.out(clock_1_out));
  not not_1 (not_1_out, clock_1_out);
  T_Flip_Flop t_ff_1 (
    .clk(clock_1_out), .T(1'b1), .Q(out_8[0]), .Qn(t_ff_1_qn), .reset(and_1_out));  // open: preset, en
  T_Flip_Flop t_ff_2 (.clk(t_ff_1_qn), .T(1'b1), .Q(out_8[1]), .Qn(t_ff_2_qn), .reset(and_1_out));  // open: preset, en
  and and_1 (and_1_out, out_8[0], ~out_8[1], out_8[2]);  // AND_Gate
  T_Flip_Flop t_ff_3 (.clk(t_ff_2_qn), .T(1'b1), .Q(out_8[2]), .reset(and_1_out));  // open: Qn, preset, en
  Multiplexer #(.select(3), .width(2)) multiplexer_1 (
    .in0(2'b00), .in1(2'b11), .in2(2'b01), .in3(2'b10), .in4(2'b11), .out(out_6), .sel(out_8), .en(1'b1));  // open: in5, in6, in7
  and and_2 (and_2_out, out_6[1], ~out_6[0], not_1_out);  // AND_Gate
  ejercicio_3 ejercicio_3_1 (
    .B0(in_1), .B1(in_2), .B2(in_3), .B3(in_4), .selector_mux(out_6), .reloj(not_1_out), .clear(and_2_out),
    .salida(out_5));

  assign out_7 = out_6;
endmodule

module ejercicio_4 (
);

  wire and_1_out, and_2_out, clock_1_out, or_1_out, or_2_out, q0_q, q1_q, q2_q;

  Clock clock_1 (.out(clock_1_out));
  or or_1 (or_1_out, ~q1_q, q0_q);  // OR_Gate
  J_K_Flip_Flop q2 (.J(or_1_out), .clk(clock_1_out), .K(1'b1), .Q(q2_q));  // open: Qn, preset, en, reset
  and and_1 (and_1_out, q2_q, ~q0_q);  // AND_Gate
  or or_2 (or_2_out, q2_q, ~q0_q);  // OR_Gate
  J_K_Flip_Flop q1 (.J(and_1_out), .clk(clock_1_out), .K(or_2_out), .Q(q1_q));  // open: Qn, preset, en, reset
  and and_2 (and_2_out, q2_q, ~q1_q);  // AND_Gate
  J_K_Flip_Flop q0 (.J(and_2_out), .clk(clock_1_out), .K(and_2_out), .Q(q0_q));  // open: Qn, preset, en, reset
endmodule

module ejercicio_5 (
  output S0,
  output S2,
  output S1
);

  wire and_1_out, and_2_out, and_3_out, and_4_out, and_5_out, and_6_out, and_8_out, and_9_out, and_10_out,
       and_11_out, and_12_out, C0_q, C1_q, C2_q, C3_q, clock_1_out, not_1_out, not_2_out, not_3_out,
       not_4_out, or_2_out, or_3_out, or_4_out, or_5_out;

  and and_1 (and_1_out, ~C3_q, C1_q, ~C0_q);  // AND_Gate
  and and_2 (and_2_out, C2_q, C1_q, ~C0_q);  // AND_Gate
  J_K_Flip_Flop C3 (.J(1'b1), .clk(not_1_out), .K(1'b1), .Q(C3_q));  // open: Qn, preset, en, reset
  not not_1 (not_1_out, C2_q);
  and and_3 (and_3_out, C3_q, ~C2_q, ~C1_q);  // AND_Gate
  and and_4 (and_4_out, C3_q, C2_q, C0_q);
  or or_1 (S2, and_1_out, and_2_out, and_4_out, and_3_out, and_5_out, and_6_out);
  and and_5 (and_5_out, C3_q, ~C1_q, C0_q);  // AND_Gate
  and and_6 (and_6_out, C3_q, ~C2_q, C0_q);  // AND_Gate
  J_K_Flip_Flop C2 (.J(1'b1), .clk(not_2_out), .K(1'b1), .Q(C2_q));  // open: Qn, preset, en, reset
  not not_2 (not_2_out, C1_q);
  J_K_Flip_Flop C1 (.J(1'b1), .clk(not_3_out), .K(1'b1), .Q(C1_q));  // open: Qn, preset, en, reset
  not not_3 (not_3_out, C0_q);
  or or_2 (or_2_out, C1_q, C0_q);
  or or_3 (or_3_out, ~C1_q, ~C0_q);  // OR_Gate
  or or_4 (or_4_out, ~C3_q, ~C2_q);  // OR_Gate
  and and_7 (S1, or_2_out, or_4_out, or_3_out, or_5_out);
  Clock clock_1 (.out(clock_1_out));
  or or_5 (or_5_out, ~C1_q, ~C3_q);  // OR_Gate
  J_K_Flip_Flop C0 (.J(1'b1), .clk(not_4_out), .K(1'b1), .Q(C0_q));  // open: Qn, preset, en, reset
  not not_4 (not_4_out, clock_1_out);
  and and_8 (and_8_out, ~C1_q, C0_q);  // AND_Gate
  and and_9 (and_9_out, C2_q, ~C1_q);  // AND_Gate
  and and_10 (and_10_out, C1_q, ~C0_q);  // AND_Gate
  and and_11 (and_11_out, C3_q, ~C2_q);  // AND_Gate
  or or_6 (S0, and_8_out, and_9_out, and_11_out, and_10_out, and_12_out);
  and and_12 (and_12_out, ~C3_q, C0_q);  // AND_Gate
endmodule
