// Logisim project boletin 1 .circ as structural Verilog: 6 circuits, main circuit Ejercicio 1
module Ejercicio_1 (
  input  A,
  input  B,
  input  C,
  input  D,
  output SA,
  output SB,
  output SC,
  output SD
);

  wire and_1_out, and_2_out, and_3_out, and_4_out, and_5_out, and_6_out, and_7_out, and_8_out, and_9_out,
       and_10_out, and_11_out, and_12_out, and_13_out, not_1_out, not_2_out, not_3_out, not_4_out, not_5_out,
       not_6_out, not_7_out, not_8_out, not_9_out, not_10_out, not_11_out, not_12_out, not_13_out,
       not_14_out, not_15_out, not_16_out, not_17_out, not_18_out, not_19_out, not_20_out, not_21_out,
       not_22_out, not_23_out, not_24_out, not_25_out, not_26_out, not_27_out;

  not not_1 (not_1_out, A);
  not not_2 (not_2_out, B);
  not not_3 (not_3_out, A);
  not not_4 (not_4_out, C);
  not not_5 (not_5_out, B);
  not not_6 (not_6_out, C);
  not not_7 (not_7_out, A);
  not not_8 (not_8_out, B);
  not not_9 (not_9_out, A);
  not not_10 (not_10_out, C);
  not not_11 (not_11_out, D);
  not not_12 (not_12_out, B);
  not not_13 (not_13_out, C);
  not not_14 (not_14_out, B);
  not not_15 (not_15_out, D);
  not not_16 (not_16_out, B);
  not not_17 (not_17_out, C);
  not not_18 (not_18_out, B);
  not not_19 (not_19_out, D);
  not not_20 (not_20_out, C);
  not not_21 (not_21_out, D);
  not not_22 (not_22_out, A);
  not not_23 (not_23_out, B);
  not not_24 (not_24_out, A);
  not not_25 (not_25_out, C);
  not not_26 (not_26_out, A);
  not not_27 (not_27_out, D);
  and and_1 (and_1_out, not_1_out, not_2_out, C);
  and and_2 (and_2_out, not_3_out, B, not_4_out);
  and and_3 (and_3_out, A, not_5_out, not_6_out);
  and and_4 (and_4_out, not_7_out, not_8_out, D);
  and and_5 (and_5_out, not_9_out, B, not_10_out, not_11_out);
  and and_6 (and_6_out, not_12_out, not_13_out, D);
  and and_7 (and_7_out, A, not_14_out, C, not_15_out);
  and and_8 (and_8_out, not_16_out, not_17_out, D);
  and and_9 (and_9_out, not_18_out, C, not_19_out);
  and and_10 (and_10_out, A, B, not_20_out, not_21_out);
  and and_11 (and_11_out, not_22_out, not_23_out, C, D);
  and and_12 (and_12_out, not_24_out, B, not_25_out, D);
  and and_13 (and_13_out, not_26_out, B, C, not_27_out);
  or or_1 (SA, and_1_out, and_2_out, and_3_out);
  or or_2 (SB, and_4_out, and_5_out, and_6_out, and_7_out);
  or or_3 (SC, and_8_out, and_9_out, and_10_out);
  or or_4 (SD, and_11_out, and_12_out, and_13_out);
endmodule

module ejercicio_2_parte_1 (
  input  b1,
  input  b2,
  input  b3,
  input  b4,
  output ERROR
);

  wire and_1_out, and_2_out;

  and and_1 (and_1_out, b1, b2);
  and and_2 (and_2_out, b1, b3);
  or or_1 (ERROR, and_1_out, and_2_out);

  // Notes on the sheet:
  //   Puertas AND OR y NOT
endmodule

module ejercicio_3 (
  input  b1,
  input  b2,
  input  b3,
  input  b4,
  input  b5,
  input  b6,
  input  b7,
  input  b8,
  output ERROR
);

  wire ejercicio_2_parte_1_1_error, ejercicio_2_parte_1_2_error;

  ejercicio_2_parte_1 ejercicio_2_parte_1_1 (.b1(b1), .b2(b2), .b3(b3), .b4(b4), .ERROR(ejercicio_2_parte_1_1_error));
  ejercicio_2_parte_1 ejercicio_2_parte_1_2 (.b1(b5), .b2(b6), .b3(b7), .b4(b8), .ERROR(ejercicio_2_parte_1_2_error));
  or or_1 (ERROR, ejercicio_2_parte_1_1_error, ejercicio_2_parte_1_2_error);
endmodule

module ejercicio_2_parte_2 (
  input  b1,
  input  b2,
  input  b3,
  input  b4,
  output ERROR
);

  wire nor_1_out, nor_2_out;

  nor nor_1 (nor_1_out, b1, b1);
  nor nor_2 (nor_2_out, b2, b3);
  nor nor_3 (ERROR, nor_1_out, nor_2_out);
endmodule

module ejercicio_4 (
  input  s1,
  input  s2,
  input  INTERRUPTOR,
  output m1,
  output m2
);

  wire nand_1_out, nand_2_out, nand_3_out, nand_4_out;

  nand nand_1 (nand_1_out, INTERRUPTOR, s1);
  nand nand_2 (nand_2_out, s1, INTERRUPTOR);
  nand nand_3 (nand_3_out, s2, INTERRUPTOR);
  nand nand_4 (nand_4_out, s2, INTERRUPTOR);
  nand nand_5 (m1, nand_1_out, nand_2_out);
  nand nand_6 (m2, nand_3_out, nand_4_out);
endmodule

module ejercicio_5 (
  input  t1,
  input  t0,
  input  noche_dia,
  input  ahorro,
  output Aire_acondicionado,
  output \calefacción 
);

  wire not_1_out, not_2_out, not_3_out, not_4_out, not_5_out, or_1_out, or_2_out;

  not not_1 (not_1_out, ahorro);
  not not_2 (not_2_out, t0);
  not not_3 (not_3_out, ahorro);
  or or_1 (or_1_out, not_1_out, not_2_out);
  or or_2 (or_2_out, not_3_out, noche_dia);
  not not_4 (not_4_out, t1);
  not not_5 (not_5_out, t0);
  and and_1 (Aire_acondicionado, t1, or_1_out);
  and and_2 (\calefacción , not_4_out, not_5_out, or_2_out);
endmodule
